// Digital circuit ALU.dig as structural Verilog
module ALU (
  input  [31:0] PC,
  input  [3:0] InstType,
  input  [2:0] InstSubType,
  input  InstSubSubType,
  input  [4:0] rd,
  input  [31:0] imm,
  input  [4:0] shamt,
  input  [31:0] rs1_val_t_plus_1,
  input  [31:0] rs2_val_t_plus_1,
  output [4:0] Reg,
  output [31:0] D,
  output C
);

  wire decoder_1_out_1, decoder_1_out_2, decoder_1_out_3, decoder_1_out_4, decoder_1_out_6, decoder_1_out_7,
       decoder_1_out_8, decoder_1_out_9, delay_15_out, priorityencoder_1_any;
  wire [0:0] slt_lt, slti_lt, sltiu_lt, sltu_lt;
  wire [3:0] delay_2_out, delay_5_out, delay_8_out, delay_12_out, delay_13_out, delay_16_out;
  wire [4:0] delay_1_out, delay_7_out, delay_14_out;
  wire [5:0] delay_4_out;
  wire [31:0] add_s, addi_s, and_1_out, and_2_out, auipc_s, delay_3_out, delay_9_out, delay_10_out,
       delay_11_out, delay_17_out, delay_18_out, delay_19_out, jal_jalr_rd_s, multiplexer_1_out,
       multiplexer_2_out, or_1_out, or_2_out, sll_out, slli_out, sra_out, srai_out, srl_out, srli_out, sub_s,
       xor_1_out, xor_2_out;

  Delay #(.Bits(5)) delay_1 (.in(rd), .out(delay_1_out));
  Decoder #(.Selector_Bits(4)) decoder_1 (
    .sel(InstType), .out_1(decoder_1_out_1), .out_2(decoder_1_out_2), .out_3(decoder_1_out_3),
    .out_4(decoder_1_out_4), .out_6(decoder_1_out_6), .out_7(decoder_1_out_7), .out_8(decoder_1_out_8),
    .out_9(decoder_1_out_9));  // open: out_0, out_5, out_10, out_11, out_12, out_13, out_14, out_15
  Delay #(.Bits(4)) delay_2 (.in(InstType), .out(delay_2_out));
  Add #(.Bits(32)) auipc (.a(imm), .b(PC), .c_i(1'b0), .s(auipc_s));  // open: c_o
  Add #(.Bits(32)) jal_jalr_rd (.a(32'h4), .b(PC), .c_i(1'b0), .s(jal_jalr_rd_s));  // open: c_o
  Delay #(.Bits(32)) delay_3 (.in(imm), .out(delay_3_out));
  Delay #(.Bits(6)) delay_4 (.in({1'b0, shamt}), .out(delay_4_out));
  Delay #(.Bits(3)) delay_5 (.in(InstSubType), .out(delay_5_out[2:0]));
  Delay delay_6 (.in(InstSubSubType), .out(delay_5_out[3]));
  Delay #(.Bits(5)) delay_7 (.in(delay_1_out), .out(delay_7_out));
  PriorityEncoder #(.Selector_Bits(4)) priorityencoder_1 (
    .in0(1'b0), .in1(decoder_1_out_1), .in2(decoder_1_out_2), .in3(decoder_1_out_3), .in4(decoder_1_out_4),
    .in5(1'b0), .in6(decoder_1_out_6), .in7(decoder_1_out_7), .in8(decoder_1_out_8), .in9(decoder_1_out_9),
    .in10(1'b0), .in11(1'b0), .in12(1'b0), .in13(1'b0), .in14(1'b0), .in15(1'b0), .any(priorityencoder_1_any));  // open: num
  Delay #(.Bits(4)) delay_8 (.in(delay_2_out), .out(delay_8_out));
  Delay #(.Bits(32)) delay_9 (.in(delay_3_out), .out(delay_9_out));
  Delay #(.Bits(32)) delay_10 (.in(auipc_s), .out(delay_10_out));
  Delay #(.Bits(32)) delay_11 (.in(jal_jalr_rd_s), .out(delay_11_out));
  Delay #(.Bits(4)) delay_12 (.in(delay_5_out), .out(delay_12_out));
  Add #(.Bits(32)) addi (.a(rs1_val_t_plus_1), .b(delay_3_out), .c_i(1'b0), .s(addi_s));  // open: c_o
  Comparator #(.Signed("true"), .Bits(32)) slti (
    .a(rs1_val_t_plus_1), .b(delay_3_out), .lt(slti_lt[0]));  // open: gt, eq
  Comparator #(.Bits(32)) sltiu (.a(rs1_val_t_plus_1), .b(delay_3_out), .lt(sltiu_lt[0]));  // open: gt, eq
  assign xor_1_out = rs1_val_t_plus_1 ^ delay_3_out;  // XOr xor_1, 32 bits wide
  assign or_1_out = rs1_val_t_plus_1 | delay_3_out;  // Or or_1, 32 bits wide
  assign and_1_out = rs1_val_t_plus_1 & delay_3_out;  // And and_1, 32 bits wide
  BarrelShifter #(.Bits(32)) slli (.in(rs1_val_t_plus_1), .shift(delay_4_out), .out(slli_out));
  BarrelShifter #(.Bits(32), .direction("right")) srli (.in(rs1_val_t_plus_1), .shift(delay_4_out), .out(srli_out));
  BarrelShifter #(.Bits(32), .barrelShifterMode("arithmetic"), .barrelSigned("true"), .direction("right")) srai (
    .in(rs1_val_t_plus_1), .shift({1'b0, delay_4_out}), .out(srai_out));
  Delay #(.Bits(4)) delay_13 (.in(delay_5_out), .out(delay_13_out));
  Add #(.Bits(32)) add (.a(rs1_val_t_plus_1), .b(rs2_val_t_plus_1), .c_i(1'b0), .s(add_s));  // open: c_o
  Sub #(.Bits(32)) sub (.a(rs1_val_t_plus_1), .b(rs2_val_t_plus_1), .c_i(1'b0), .s(sub_s));  // open: c_o
  BarrelShifter #(.Bits(32)) sll (.in(rs1_val_t_plus_1), .shift({1'b0, rs2_val_t_plus_1[4:0]}), .out(sll_out));
  Comparator #(.Signed("true"), .Bits(32)) slt (
    .a(rs1_val_t_plus_1), .b(rs2_val_t_plus_1), .lt(slt_lt[0]));  // open: gt, eq
  Comparator #(.Bits(32)) sltu (.a(rs1_val_t_plus_1), .b(rs2_val_t_plus_1), .lt(sltu_lt[0]));  // open: gt, eq
  assign xor_2_out = rs1_val_t_plus_1 ^ rs2_val_t_plus_1;  // XOr xor_2, 32 bits wide
  BarrelShifter #(.Bits(32), .direction("right")) srl (
    .in(rs1_val_t_plus_1), .shift({1'b0, rs2_val_t_plus_1[4:0]}), .out(srl_out));
  BarrelShifter #(.Bits(32), .barrelShifterMode("arithmetic"), .barrelSigned("true"), .direction("right")) sra (
    .in(rs1_val_t_plus_1), .shift({2'b00, rs2_val_t_plus_1[4:0]}), .out(sra_out));
  assign or_2_out = rs1_val_t_plus_1 | rs2_val_t_plus_1;  // Or or_2, 32 bits wide
  assign and_2_out = rs1_val_t_plus_1 & rs2_val_t_plus_1;  // And and_2, 32 bits wide
  Delay #(.Bits(5)) delay_14 (.in(delay_7_out), .out(delay_14_out));
  Delay delay_15 (.in(priorityencoder_1_any), .out(delay_15_out));
  Delay #(.Bits(4)) delay_16 (.in(delay_8_out), .out(delay_16_out));
  Delay #(.Bits(32)) delay_17 (.in(delay_9_out), .out(delay_17_out));
  Delay #(.Bits(32)) delay_18 (.in(delay_10_out), .out(delay_18_out));
  Delay #(.Bits(32)) delay_19 (.in(delay_11_out), .out(delay_19_out));
  Multiplexer #(.Selector_Bits(4), .Bits(32)) multiplexer_1 (
    .sel(delay_12_out), .in_0(addi_s), .in_1(slli_out), .in_2({{31{1'b0}}, slti_lt[0]}),
    .in_3({{31{1'b0}}, sltiu_lt[0]}), .in_4(xor_1_out), .in_5(srli_out), .in_6(or_1_out), .in_7(and_1_out),
    .in_8(addi_s), .in_9(slli_out), .in_10({{31{1'b0}}, slti_lt[0]}), .in_11({{31{1'b0}}, sltiu_lt[0]}),
    .in_12(xor_1_out), .in_13(srai_out), .in_14(or_1_out), .in_15(and_1_out), .out(multiplexer_1_out));
  Multiplexer #(.Selector_Bits(4), .Bits(32)) multiplexer_2 (
    .sel(delay_13_out), .in_0(add_s), .in_1(sll_out), .in_2({{31{1'b0}}, slt_lt[0]}),
    .in_3({{31{1'b0}}, sltu_lt[0]}), .in_4(xor_2_out), .in_5(srl_out), .in_6(or_2_out), .in_7(and_2_out),
    .in_8(sub_s), .in_9(sll_out), .in_10({{31{1'b0}}, slt_lt[0]}), .in_11({{31{1'b0}}, sltu_lt[0]}),
    .in_12(xor_2_out), .in_13(sra_out), .in_14(or_2_out), .in_15(and_2_out), .out(multiplexer_2_out));
  Delay #(.Bits(5)) delay_20 (.in(delay_14_out), .out(Reg));
  Delay delay_21 (.in(delay_15_out), .out(C));
  Multiplexer #(.Selector_Bits(4), .Bits(32)) multiplexer_3 (
    .sel(delay_16_out), .in_0({32{1'b0}}), .in_1(delay_17_out), .in_2(delay_18_out), .in_3(delay_19_out),
    .in_4(delay_19_out), .in_5({32{1'b0}}), .in_6({32{1'b0}}), .in_7({32{1'b0}}), .in_8(multiplexer_1_out),
    .in_9(multiplexer_2_out), .in_10({32{1'b0}}), .in_11({32{1'b0}}), .in_12({32{1'b0}}), .in_13({32{1'b0}}),
    .in_14({32{1'b0}}), .in_15({32{1'b0}}), .out(D));

  // Notes on the sheet:
  //   lui
  //   xori
  //   ori
  //   andi
endmodule
