// Digital circuit LSU.dig as structural Verilog
module LSU (
  input  [7:0] D_RAM,
  input  [3:0] InstType,
  input  [2:0] InstSubType,
  input  [31:0] imm,
  input  Pwr,
  input  [4:0] rd,
  input  [31:0] rs1_val_t_plus_1,
  input  [31:0] rs2_val_t_plus_1,
  output [31:0] A_RAM,
  output [7:0] Din_RAM,
  output C_RAM,
  output ld_RAM,
  output [4:0] Reg,
  output [31:0] D,
  output C
);

  wire and_1_out, and_2_out, and_3_out, and_4_out, and_5_out, and_6_out, and_7_out, decoder_1_out_7,
       delay_4_out, delay_9_out, delay_11_out, delay_12_out, delay_13_out, delay_14_out, delay_15_out,
       delay_20_out, delay_22_out, delay_23_out, delay_24_out, delay_26_out, delay_33_out, delay_34_out,
       delay_35_out, delay_45_out, delay_46_out, delay_47_out, delay_48_out, delay_49_out, delay_50_out,
       delay_51_out, delay_52_out, delay_53_out, delay_54_out, delay_55_out, or_1_out, or_5_out,
       priorityencoder_1_any, priorityencoder_2_any;
  wire [0:0] delay_27_out;
  wire [1:1] delay_28_out, delay_29_out;
  wire [2:0] delay_3_out, delay_39_out, multiplexer_2_out;
  wire [3:0] delay_10_out, delay_25_out, delay_42_out, delay_43_out, delay_44_out, multiplexer_4_out;
  wire [3:3] decoder_1_out_6;
  wire [4:0] delay_2_out, delay_21_out, delay_36_out, delay_37_out, delay_38_out, multiplexer_1_out,
       multiplexer_3_out;
  wire [7:0] delay_5_out, delay_6_out, delay_7_out, delay_8_out, delay_16_out, delay_17_out, delay_18_out,
       delay_19_out, delay_30_out, delay_31_out, delay_32_out, register_1_q, register_2_q, register_3_q,
       register_4_q;
  wire [31:0] add_1_s, Addr_q, bitextender_1_out, bitextender_2_out, delay_1_out, or_2_out;

  Delay #(.Bits(32)) delay_1 (.in(imm), .out(delay_1_out));
  Decoder #(.Selector_Bits(4)) decoder_1 (
    .sel(InstType), .out_6(decoder_1_out_6[3]), .out_7(decoder_1_out_7));  // open: out_0, out_1, out_2, out_3, out_4, out_5, out_8, out_9, out_10, out_11, out_12, out_13, out_14, out_15
  Delay #(.Bits(5)) delay_2 (.in(rd), .out(delay_2_out));
  Delay #(.Bits(3)) delay_3 (.in(InstSubType), .out(delay_3_out));
  PriorityEncoder priorityencoder_1 (
    .in0(delay_3_out[0]), .in1(delay_3_out[1]), .any(priorityencoder_1_any));  // open: num
  Delay delay_4 (.in(delay_3_out[1]), .out(delay_4_out));
  Add #(.Bits(32)) add_1 (.a(delay_1_out), .b(rs1_val_t_plus_1), .c_i(1'b0), .s(add_1_s));  // open: c_o
  PriorityEncoder priorityencoder_2 (
    .in0(decoder_1_out_6[3]), .in1(decoder_1_out_7), .any(priorityencoder_2_any));  // open: num
  Delay #(.Bits(8)) delay_5 (.in(rs2_val_t_plus_1[7:0]), .out(delay_5_out));
  Delay #(.Bits(8)) delay_6 (.in(rs2_val_t_plus_1[15:8]), .out(delay_6_out));
  Delay #(.Bits(8)) delay_7 (.in(rs2_val_t_plus_1[23:16]), .out(delay_7_out));
  Delay #(.Bits(8)) delay_8 (.in(rs2_val_t_plus_1[31:24]), .out(delay_8_out));
  or or_1 (or_1_out, delay_3_out[0], delay_3_out[1]);
  Delay delay_9 (.in(decoder_1_out_7), .out(delay_9_out));
  Multiplexer #(.Bits(5)) multiplexer_1 (
    .sel(decoder_1_out_6[3]), .in_0({5{1'b0}}), .in_1(delay_2_out), .out(multiplexer_1_out));
  and and_1 (and_1_out, ~delay_3_out[0], decoder_1_out_6[3], ~delay_3_out[1]);  // And
  Multiplexer #(.Bits(3)) multiplexer_2 (
    .sel(decoder_1_out_6[3]), .in_0(3'b000), .in_1(delay_3_out), .out(multiplexer_2_out));
  Delay #(.Bits(4)) delay_10 (.in({decoder_1_out_6[3], delay_3_out}), .out(delay_10_out));
  Delay delay_11 (.in(delay_3_out[1]), .out(delay_11_out));
  Delay delay_12 (.in(decoder_1_out_6[3]), .out(delay_12_out));
  Delay delay_13 (.in(priorityencoder_1_any), .out(delay_13_out));
  Delay delay_14 (.in(delay_4_out), .out(delay_14_out));
  Delay delay_15 (.in(delay_4_out), .out(delay_15_out));
  Register #(.Bits(32)) Addr (.D(add_1_s), .C(priorityencoder_2_any), .en(Pwr), .Q(Addr_q));
  Delay #(.Bits(8)) delay_16 (.in(delay_5_out), .out(delay_16_out));
  Delay #(.Bits(8)) delay_17 (.in(delay_6_out), .out(delay_17_out));
  Delay #(.Bits(8)) delay_18 (.in(delay_7_out), .out(delay_18_out));
  Delay #(.Bits(8)) delay_19 (.in(delay_8_out), .out(delay_19_out));
  Delay delay_20 (.in(delay_9_out), .out(delay_20_out));
  and and_2 (and_2_out, delay_9_out, or_1_out);
  and and_3 (and_3_out, delay_9_out, delay_11_out);
  and and_4 (and_4_out, delay_9_out, delay_11_out);
  Delay #(.Bits(5)) delay_21 (.in(multiplexer_1_out), .out(delay_21_out));
  Delay delay_22 (.in(and_1_out), .out(delay_22_out));
  Delay delay_23 (.in(multiplexer_2_out[0]), .out(delay_23_out));
  Delay delay_24 (.in(multiplexer_2_out[1]), .out(delay_24_out));
  Delay #(.Bits(4)) delay_25 (.in(delay_10_out), .out(delay_25_out));
  Delay delay_26 (.in(delay_12_out), .out(delay_26_out));
  and and_5 (and_5_out, or_1_out, delay_12_out);
  and and_6 (and_6_out, delay_12_out, delay_11_out);
  and and_7 (and_7_out, delay_11_out, delay_12_out);
  Delay delay_27 (.in(delay_13_out), .out(delay_27_out[0]));
  Delay #(.delayTime(3)) delay_28 (.in(delay_14_out), .out(delay_28_out[1]));
  Delay #(.delayTime(5)) delay_29 (.in(delay_15_out), .out(delay_29_out[1]));
  Delay #(.Bits(8), .delayTime(2)) delay_30 (.in(delay_17_out), .out(delay_30_out));
  Delay #(.Bits(8), .delayTime(4)) delay_31 (.in(delay_18_out), .out(delay_31_out));
  Delay #(.Bits(8), .delayTime(6)) delay_32 (.in(delay_19_out), .out(delay_32_out));
  Delay #(.delayTime(2)) delay_33 (.in(and_2_out), .out(delay_33_out));
  Delay #(.delayTime(4)) delay_34 (.in(and_3_out), .out(delay_34_out));
  Delay #(.delayTime(6)) delay_35 (.in(and_4_out), .out(delay_35_out));
  Delay #(.Bits(5), .delayTime(2)) delay_36 (.in(delay_21_out), .out(delay_36_out));
  Delay #(.Bits(5), .delayTime(4)) delay_37 (.in(delay_21_out), .out(delay_37_out));
  Delay #(.Bits(5), .delayTime(8)) delay_38 (.in(delay_21_out), .out(delay_38_out));
  Delay #(.delayTime(2)) delay_39 (.in(delay_22_out), .out(delay_39_out[0]));
  Delay #(.delayTime(4)) delay_40 (.in(delay_23_out), .out(delay_39_out[1]));
  Delay #(.delayTime(8)) delay_41 (.in(delay_24_out), .out(delay_39_out[2]));
  Delay #(.Bits(4), .delayTime(2)) delay_42 (.in(delay_25_out), .out(delay_42_out));
  Delay #(.Bits(4), .delayTime(4)) delay_43 (.in(delay_25_out), .out(delay_43_out));
  Delay #(.Bits(4), .delayTime(8)) delay_44 (.in(delay_25_out), .out(delay_44_out));
  Delay #(.delayTime(2)) delay_45 (.in(and_5_out), .out(delay_45_out));
  Delay #(.delayTime(4)) delay_46 (.in(and_6_out), .out(delay_46_out));
  Delay #(.delayTime(6)) delay_47 (.in(and_7_out), .out(delay_47_out));
  assign or_2_out = {{31{1'b0}}, delay_27_out[0]} | {{30{1'b0}}, delay_28_out[1], 1'b0} | {{30{1'b0}}, {2{delay_29_out[1]}}};  // Or or_2, 32 bits wide
  Add #(.Bits(32)) add_2 (.a(or_2_out), .b(Addr_q), .c_i(1'b0), .s(A_RAM));  // open: c_o
  assign Din_RAM = delay_16_out | delay_30_out | delay_31_out | delay_32_out;  // Or or_3, 8 bits wide
  or or_4 (C_RAM, delay_20_out, delay_33_out, delay_34_out, delay_35_out);
  Multiplexer #(.Selector_Bits(3), .Bits(5)) multiplexer_3 (
    .sel(delay_39_out), .in_0({5{1'b0}}), .in_1(delay_36_out), .in_2(delay_37_out), .in_3({5{1'b0}}),
    .in_4(delay_38_out), .in_5({5{1'b0}}), .in_6({5{1'b0}}), .in_7({5{1'b0}}), .out(multiplexer_3_out));
  or or_5 (or_5_out, delay_39_out[0], delay_39_out[1], delay_39_out[2]);
  Multiplexer #(.Selector_Bits(3), .Bits(4)) multiplexer_4 (
    .sel(delay_39_out), .in_0(4'b0000), .in_1(delay_42_out), .in_2(delay_43_out), .in_3(4'b0000),
    .in_4(delay_44_out), .in_5(4'b0000), .in_6(4'b0000), .in_7(4'b0000), .out(multiplexer_4_out));
  Delay delay_48 (.in(delay_26_out), .out(delay_48_out));
  Delay delay_49 (.in(delay_45_out), .out(delay_49_out));
  or or_6 (ld_RAM, delay_26_out, delay_45_out, delay_46_out, delay_47_out);
  Delay delay_50 (.in(delay_46_out), .out(delay_50_out));
  Delay delay_51 (.in(delay_47_out), .out(delay_51_out));
  Delay delay_52 (.in(delay_48_out), .out(delay_52_out));
  Delay delay_53 (.in(delay_49_out), .out(delay_53_out));
  Delay delay_54 (.in(delay_50_out), .out(delay_54_out));
  Delay delay_55 (.in(delay_51_out), .out(delay_55_out));
  Register #(.Bits(8)) register_1 (.D(D_RAM), .C(delay_52_out), .en(Pwr), .Q(register_1_q));
  Register #(.Bits(8)) register_2 (.D(D_RAM), .C(delay_53_out), .en(Pwr), .Q(register_2_q));
  Register #(.Bits(8)) register_3 (.D(D_RAM), .C(delay_54_out), .en(Pwr), .Q(register_3_q));
  Register #(.Bits(8)) register_4 (.D(D_RAM), .C(delay_55_out), .en(Pwr), .Q(register_4_q));
  BitExtender #(.outputBits(32)) bitextender_1 (.in(register_1_q), .out(bitextender_1_out));
  BitExtender #(.inputBits(16), .outputBits(32)) bitextender_2 (
    .in({register_2_q, register_1_q}), .out(bitextender_2_out));
  Delay #(.Bits(5)) delay_56 (.in(multiplexer_3_out), .out(Reg));
  Delay delay_57 (.in(or_5_out), .out(C));
  Multiplexer #(.Selector_Bits(4), .Bits(32)) multiplexer_5 (
    .sel(multiplexer_4_out), .in_0({32{1'b0}}), .in_1({32{1'b0}}), .in_2({32{1'b0}}), .in_3({32{1'b0}}),
    .in_4({32{1'b0}}), .in_5({32{1'b0}}), .in_6({32{1'b0}}), .in_7({32{1'b0}}), .in_8(bitextender_1_out),
    .in_9(bitextender_2_out), .in_10({register_4_q, register_3_q, register_2_q, register_1_q}),
    .in_11({32{1'b0}}), .in_12({{24{1'b0}}, register_1_q}), .in_13({{16{1'b0}}, register_2_q, register_1_q}),
    .in_14({32{1'b0}}), .in_15({32{1'b0}}), .out(D));
endmodule
