// Digital circuit LSU_debug.dig as structural Verilog
module LSU_debug (
  input  [7:0] D_RAM,
  input  [3:0] InstType,
  input  [31:0] imm,
  input  [31:0] rs1_val_t_plus_1,
  input  [31:0] rs2_val_t_plus_1,
  input  Pwr,
  input  [2:0] InstSubType,
  input  [4:0] rd,
  input  b,
  output [31:0] A_RAM,
  output [7:0] Din_RAM,
  output C_RAM,
  output ld_RAM,
  output [4:0] Reg,
  output [31:0] D,
  output C
);

  wire and_1_out, and_2_out, and_3_out, and_4_out, and_5_out, and_6_out, and_7_out, decoder_1_out_7,
       delay_1_out, delay_5_out, delay_10_out, delay_12_out, delay_13_out, delay_14_out, delay_15_out,
       delay_16_out, delay_21_out, delay_23_out, delay_24_out, delay_25_out, delay_27_out, delay_34_out,
       delay_35_out, delay_36_out, delay_46_out, delay_47_out, delay_48_out, delay_49_out, delay_50_out,
       delay_51_out, delay_52_out, delay_53_out, delay_54_out, delay_55_out, delay_56_out, or_1_out,
       or_4_out, or_5_out, or_6_out, priorityencoder_1_any, priorityencoder_2_any, pulse_1_out;
  wire [0:0] delay_28_out;
  wire [1:1] delay_29_out, delay_30_out;
  wire [2:0] delay_4_out, delay_40_out, multiplexer_4_out, multiplexer_8_out;
  wire [3:0] delay_11_out, delay_26_out, delay_43_out, delay_44_out, delay_45_out, multiplexer_2_out,
       multiplexer_10_out;
  wire [3:3] decoder_1_out_6;
  wire [4:0] delay_3_out, delay_22_out, delay_37_out, delay_38_out, delay_39_out, multiplexer_3_out,
       multiplexer_7_out, multiplexer_9_out;
  wire [7:0] delay_6_out, delay_7_out, delay_8_out, delay_9_out, delay_17_out, delay_18_out, delay_19_out,
       delay_20_out, delay_31_out, delay_32_out, delay_33_out, or_3_out, ramdualport_1_d, register_1_q,
       register_2_q, register_3_q, register_4_q;
  wire [31:0] add_1_s, add_2_s, Addr_q, bitextender_1_out, bitextender_2_out, delay_2_out, multiplexer_1_out,
       multiplexer_5_out, multiplexer_6_out, or_2_out;

  pulse #(.generic("Duration := 1;")) pulse_1 (.In(b), .Out(pulse_1_out));
  Multiplexer #(.Bits(32)) multiplexer_1 (.sel(pulse_1_out), .in_0({32{1'b0}}), .in_1(imm), .out(multiplexer_1_out));
  Delay delay_1 (.in(pulse_1_out), .out(delay_1_out));
  Multiplexer #(.Bits(4)) multiplexer_2 (.sel(pulse_1_out), .in_0(4'b0000), .in_1(InstType), .out(multiplexer_2_out));
  Multiplexer #(.Bits(5)) multiplexer_3 (.sel(pulse_1_out), .in_0({5{1'b0}}), .in_1(rd), .out(multiplexer_3_out));
  Multiplexer #(.Bits(3)) multiplexer_4 (.sel(pulse_1_out), .in_0(3'b000), .in_1(InstSubType), .out(multiplexer_4_out));
  Delay #(.Bits(32)) delay_2 (.in(multiplexer_1_out), .out(delay_2_out));
  Multiplexer #(.Bits(32)) multiplexer_5 (
    .sel(delay_1_out), .in_0({32{1'b0}}), .in_1(rs1_val_t_plus_1), .out(multiplexer_5_out));
  Multiplexer #(.Bits(32)) multiplexer_6 (
    .sel(delay_1_out), .in_0({32{1'b0}}), .in_1(rs2_val_t_plus_1), .out(multiplexer_6_out));
  Decoder #(.Selector_Bits(4)) decoder_1 (
    .sel(multiplexer_2_out), .out_6(decoder_1_out_6[3]), .out_7(decoder_1_out_7));  // open: out_0, out_1, out_2, out_3, out_4, out_5, out_8, out_9, out_10, out_11, out_12, out_13, out_14, out_15
  Delay #(.Bits(5)) delay_3 (.in(multiplexer_3_out), .out(delay_3_out));
  Delay #(.Bits(3)) delay_4 (.in(multiplexer_4_out), .out(delay_4_out));
  PriorityEncoder priorityencoder_1 (
    .in0(delay_4_out[0]), .in1(delay_4_out[1]), .any(priorityencoder_1_any));  // open: num
  Delay delay_5 (.in(delay_4_out[1]), .out(delay_5_out));
  Add #(.Bits(32)) add_1 (.a(delay_2_out), .b(multiplexer_5_out), .c_i(1'b0), .s(add_1_s));  // open: c_o
  PriorityEncoder priorityencoder_2 (
    .in0(decoder_1_out_6[3]), .in1(decoder_1_out_7), .any(priorityencoder_2_any));  // open: num
  Delay #(.Bits(8)) delay_6 (.in(multiplexer_6_out[7:0]), .out(delay_6_out));
  Delay #(.Bits(8)) delay_7 (.in(multiplexer_6_out[15:8]), .out(delay_7_out));
  Delay #(.Bits(8)) delay_8 (.in(multiplexer_6_out[23:16]), .out(delay_8_out));
  Delay #(.Bits(8)) delay_9 (.in(multiplexer_6_out[31:24]), .out(delay_9_out));
  or or_1 (or_1_out, delay_4_out[0], delay_4_out[1]);
  Delay delay_10 (.in(decoder_1_out_7), .out(delay_10_out));
  Multiplexer #(.Bits(5)) multiplexer_7 (
    .sel(decoder_1_out_6[3]), .in_0({5{1'b0}}), .in_1(delay_3_out), .out(multiplexer_7_out));
  and and_1 (and_1_out, ~delay_4_out[0], decoder_1_out_6[3], ~delay_4_out[1]);  // And
  Multiplexer #(.Bits(3)) multiplexer_8 (
    .sel(decoder_1_out_6[3]), .in_0(3'b000), .in_1(delay_4_out), .out(multiplexer_8_out));
  Delay #(.Bits(4)) delay_11 (.in({decoder_1_out_6[3], delay_4_out}), .out(delay_11_out));
  Delay delay_12 (.in(delay_4_out[1]), .out(delay_12_out));
  Delay delay_13 (.in(decoder_1_out_6[3]), .out(delay_13_out));
  Delay delay_14 (.in(priorityencoder_1_any), .out(delay_14_out));
  Delay delay_15 (.in(delay_5_out), .out(delay_15_out));
  Delay delay_16 (.in(delay_5_out), .out(delay_16_out));
  Register #(.Bits(32)) Addr (.D(add_1_s), .C(priorityencoder_2_any), .en(Pwr), .Q(Addr_q));
  Delay #(.Bits(8)) delay_17 (.in(delay_6_out), .out(delay_17_out));
  Delay #(.Bits(8)) delay_18 (.in(delay_7_out), .out(delay_18_out));
  Delay #(.Bits(8)) delay_19 (.in(delay_8_out), .out(delay_19_out));
  Delay #(.Bits(8)) delay_20 (.in(delay_9_out), .out(delay_20_out));
  Delay delay_21 (.in(delay_10_out), .out(delay_21_out));
  and and_2 (and_2_out, delay_10_out, or_1_out);
  and and_3 (and_3_out, delay_10_out, delay_12_out);
  and and_4 (and_4_out, delay_10_out, delay_12_out);
  Delay #(.Bits(5)) delay_22 (.in(multiplexer_7_out), .out(delay_22_out));
  Delay delay_23 (.in(and_1_out), .out(delay_23_out));
  Delay delay_24 (.in(multiplexer_8_out[0]), .out(delay_24_out));
  Delay delay_25 (.in(multiplexer_8_out[1]), .out(delay_25_out));
  Delay #(.Bits(4)) delay_26 (.in(delay_11_out), .out(delay_26_out));
  Delay delay_27 (.in(delay_13_out), .out(delay_27_out));
  and and_5 (and_5_out, or_1_out, delay_13_out);
  and and_6 (and_6_out, delay_13_out, delay_12_out);
  and and_7 (and_7_out, delay_12_out, delay_13_out);
  Delay delay_28 (.in(delay_14_out), .out(delay_28_out[0]));
  Delay #(.delayTime(3)) delay_29 (.in(delay_15_out), .out(delay_29_out[1]));
  Delay #(.delayTime(5)) delay_30 (.in(delay_16_out), .out(delay_30_out[1]));
  Delay #(.Bits(8), .delayTime(2)) delay_31 (.in(delay_18_out), .out(delay_31_out));
  Delay #(.Bits(8), .delayTime(4)) delay_32 (.in(delay_19_out), .out(delay_32_out));
  Delay #(.Bits(8), .delayTime(6)) delay_33 (.in(delay_20_out), .out(delay_33_out));
  Delay #(.delayTime(2)) delay_34 (.in(and_2_out), .out(delay_34_out));
  Delay #(.delayTime(4)) delay_35 (.in(and_3_out), .out(delay_35_out));
  Delay #(.delayTime(6)) delay_36 (.in(and_4_out), .out(delay_36_out));
  Delay #(.Bits(5), .delayTime(2)) delay_37 (.in(delay_22_out), .out(delay_37_out));
  Delay #(.Bits(5), .delayTime(4)) delay_38 (.in(delay_22_out), .out(delay_38_out));
  Delay #(.Bits(5), .delayTime(8)) delay_39 (.in(delay_22_out), .out(delay_39_out));
  Delay #(.delayTime(2)) delay_40 (.in(delay_23_out), .out(delay_40_out[0]));
  Delay #(.delayTime(4)) delay_41 (.in(delay_24_out), .out(delay_40_out[1]));
  Delay #(.delayTime(8)) delay_42 (.in(delay_25_out), .out(delay_40_out[2]));
  Delay #(.Bits(4), .delayTime(2)) delay_43 (.in(delay_26_out), .out(delay_43_out));
  Delay #(.Bits(4), .delayTime(4)) delay_44 (.in(delay_26_out), .out(delay_44_out));
  Delay #(.Bits(4), .delayTime(8)) delay_45 (.in(delay_26_out), .out(delay_45_out));
  Delay #(.delayTime(2)) delay_46 (.in(and_5_out), .out(delay_46_out));
  Delay #(.delayTime(4)) delay_47 (.in(and_6_out), .out(delay_47_out));
  Delay #(.delayTime(6)) delay_48 (.in(and_7_out), .out(delay_48_out));
  assign or_2_out = {{31{1'b0}}, delay_28_out[0]} | {{30{1'b0}}, delay_29_out[1], 1'b0} | {{30{1'b0}}, {2{delay_30_out[1]}}};  // Or or_2, 32 bits wide
  Add #(.Bits(32)) add_2 (.a(or_2_out), .b(Addr_q), .c_i(1'b0), .s(add_2_s));  // open: c_o
  assign or_3_out = delay_17_out | delay_31_out | delay_32_out | delay_33_out;  // Or or_3, 8 bits wide
  or or_4 (or_4_out, delay_21_out, delay_34_out, delay_35_out, delay_36_out);
  Multiplexer #(.Selector_Bits(3), .Bits(5)) multiplexer_9 (
    .sel(delay_40_out), .in_0({5{1'b0}}), .in_1(delay_37_out), .in_2(delay_38_out), .in_3({5{1'b0}}),
    .in_4(delay_39_out), .in_5({5{1'b0}}), .in_6({5{1'b0}}), .in_7({5{1'b0}}), .out(multiplexer_9_out));
  or or_5 (or_5_out, delay_40_out[0], delay_40_out[1], delay_40_out[2]);
  Multiplexer #(.Selector_Bits(3), .Bits(4)) multiplexer_10 (
    .sel(delay_40_out), .in_0(4'b0000), .in_1(delay_43_out), .in_2(delay_44_out), .in_3(4'b0000),
    .in_4(delay_45_out), .in_5(4'b0000), .in_6(4'b0000), .in_7(4'b0000), .out(multiplexer_10_out));
  Delay delay_49 (.in(delay_27_out), .out(delay_49_out));
  Delay delay_50 (.in(delay_46_out), .out(delay_50_out));
  or or_6 (or_6_out, delay_27_out, delay_46_out, delay_47_out, delay_48_out);
  Delay delay_51 (.in(delay_47_out), .out(delay_51_out));
  Delay delay_52 (.in(delay_48_out), .out(delay_52_out));
  RAMDualPort #(.AddrBits(24), .Bits(8)) ramdualport_1 (
    .A(add_2_s[23:0]), .Din(or_3_out), .str(Pwr), .C(or_4_out), .ld(or_6_out), .D(ramdualport_1_d));
  Delay delay_53 (.in(delay_49_out), .out(delay_53_out));
  Delay delay_54 (.in(delay_50_out), .out(delay_54_out));
  Delay delay_55 (.in(delay_51_out), .out(delay_55_out));
  Delay delay_56 (.in(delay_52_out), .out(delay_56_out));
  Register #(.Bits(8)) register_1 (.D(ramdualport_1_d), .C(delay_53_out), .en(Pwr), .Q(register_1_q));
  Register #(.Bits(8)) register_2 (.D(ramdualport_1_d), .C(delay_54_out), .en(Pwr), .Q(register_2_q));
  Register #(.Bits(8)) register_3 (.D(ramdualport_1_d), .C(delay_55_out), .en(Pwr), .Q(register_3_q));
  Register #(.Bits(8)) register_4 (.D(ramdualport_1_d), .C(delay_56_out), .en(Pwr), .Q(register_4_q));
  BitExtender #(.outputBits(32)) bitextender_1 (.in(register_1_q), .out(bitextender_1_out));
  BitExtender #(.inputBits(16), .outputBits(32)) bitextender_2 (
    .in({register_2_q, register_1_q}), .out(bitextender_2_out));
  Delay #(.Bits(5)) delay_57 (.in(multiplexer_9_out), .out(Reg));
  Delay delay_58 (.in(or_5_out), .out(C));
  Multiplexer #(.Selector_Bits(4), .Bits(32)) multiplexer_11 (
    .sel(multiplexer_10_out), .in_0({32{1'b0}}), .in_1({32{1'b0}}), .in_2({32{1'b0}}), .in_3({32{1'b0}}),
    .in_4({32{1'b0}}), .in_5({32{1'b0}}), .in_6({32{1'b0}}), .in_7({32{1'b0}}), .in_8(bitextender_1_out),
    .in_9(bitextender_2_out), .in_10({register_4_q, register_3_q, register_2_q, register_1_q}),
    .in_11({32{1'b0}}), .in_12({{24{1'b0}}, register_1_q}), .in_13({{16{1'b0}}, register_2_q, register_1_q}),
    .in_14({32{1'b0}}), .in_15({32{1'b0}}), .out(D));

  assign A_RAM = 32'h1;
  assign C_RAM = 1'b0;
  assign Din_RAM = 8'h1;
  assign ld_RAM = 1'b0;
endmodule
