// Digital circuit PC.dig as structural Verilog
module PC (
  input  Go,
  input  Rst,
  input  [31:0] Nxt,
  input  Pwr,
  output [31:0] Addr,
  output Done
);

  wire or_1_out;
  wire [31:0] multiplexer_1_out;

  Multiplexer #(.Bits(32)) multiplexer_1 (.sel(Rst), .in_0(Nxt), .in_1({32{1'b0}}), .out(multiplexer_1_out));
  or or_1 (or_1_out, Rst, Go);
  Register #(.Bits(32)) PC (.D(multiplexer_1_out), .C(or_1_out), .en(Pwr), .Q(Addr));
  Delay delay_1 (.in(or_1_out), .out(Done));
endmodule
