// Digital circuit RISC-V.dig as structural Verilog
module RISC_V (
  input  ON_OFF
);

  wire _1_6_steps_nxt, _2_steps_2_done, _2_steps_2_error, _2_steps_2_instsubsubtype, _2_steps_done,
       _4_steps_c, _7_13_steps_c, _7_13_steps_c_ram, _7_13_steps_ld_ram, _9_steps_done, _9_steps_oe,
       and_1_out, or_2_out, rst;
  wire [2:0] _2_steps_2_instsubype;
  wire [3:0] _2_steps_2_insttype, _2_steps_2_jmptype;
  wire [4:0] _2_steps_2_inst, _2_steps_2_rd, _2_steps_2_rs1, _2_steps_2_shamt_rs2, _4_steps_reg,
       _7_13_steps_reg, or_3_out;
  wire [7:0] _7_13_steps_din_ram, ramdualport_1_d, ROM_d;
  wire [23:0] _7_13_steps_a_ram;
  wire [31:0] _1_2_steps_rs1, _1_2_steps_rs2, _1_6_steps_jmp_val, _2_steps_2_imm, _2_steps_addr, _4_steps_d,
       _7_13_steps_d, _9_steps_a, _9_steps_val, or_1_out;
  wire [31:24] _7_13_steps_a_ram_2;

  pulse #(.generic("Duration := 1;")) pulse_1 (.In(ON_OFF), .Out(rst));
  PC _2_steps (
    .Go(_1_6_steps_nxt), .Rst(rst), .Nxt(_1_6_steps_jmp_val), .Pwr(ON_OFF), .Addr(_2_steps_addr),
    .Done(_2_steps_done));
  fetcher _9_steps (
    .Addr(_2_steps_addr), .C(_2_steps_done), .Pwr(ON_OFF), .D(ROM_d), .Val(_9_steps_val),
    .Done(_9_steps_done), .A(_9_steps_a), .OE(_9_steps_oe));
  EEPROM #(.AddrBits(24), .isProgramMemory("true"), .Bits(8)) ROM (
    .A(_9_steps_a[23:0]), .CS(ON_OFF), .WE(1'b0), .OE(_9_steps_oe), .D(ROM_d));
  decoder _2_steps_2 (
    .Val(_9_steps_val), .C(_9_steps_done), .Pwr(ON_OFF), .Done(_2_steps_2_done), .Error(_2_steps_2_error),
    .Inst(_2_steps_2_inst), .InstType(_2_steps_2_insttype), .InstSubype(_2_steps_2_instsubype),
    .InstSubSubType(_2_steps_2_instsubsubtype), .rd(_2_steps_2_rd), .rs1(_2_steps_2_rs1),
    .shamt_rs2(_2_steps_2_shamt_rs2), .imm(_2_steps_2_imm), .JmpType(_2_steps_2_jmptype));
  Stop stop_1 (.stop(and_1_out));
  and and_1 (and_1_out, _2_steps_2_done, _2_steps_2_error);
  LSU _7_13_steps (
    .D_RAM(ramdualport_1_d), .InstType(_2_steps_2_insttype), .InstSubType(_2_steps_2_instsubype),
    .imm(_2_steps_2_imm), .Pwr(ON_OFF), .rd(_2_steps_2_rd), .rs1_val_t_plus_1(_1_2_steps_rs1),
    .rs2_val_t_plus_1(_1_2_steps_rs2), .A_RAM({_7_13_steps_a_ram_2, _7_13_steps_a_ram}),
    .Din_RAM(_7_13_steps_din_ram), .C_RAM(_7_13_steps_c_ram), .ld_RAM(_7_13_steps_ld_ram),
    .Reg(_7_13_steps_reg), .D(_7_13_steps_d), .C(_7_13_steps_c));
  ALU _4_steps (
    .PC(_2_steps_addr), .InstType(_2_steps_2_insttype), .InstSubType(_2_steps_2_instsubype),
    .InstSubSubType(_2_steps_2_instsubsubtype), .rd(_2_steps_2_rd), .imm(_2_steps_2_imm),
    .shamt(_2_steps_2_shamt_rs2), .rs1_val_t_plus_1(_1_2_steps_rs1), .rs2_val_t_plus_1(_1_2_steps_rs2),
    .Reg(_4_steps_reg), .D(_4_steps_d), .C(_4_steps_c));
  registers _1_2_steps (
    .Reg(or_3_out), .D(or_1_out), .C(or_2_out), .rs1_sel(_2_steps_2_rs1), .rs2_sel(_2_steps_2_shamt_rs2),
    .Rst(rst), .Pwr(ON_OFF), .rs1(_1_2_steps_rs1), .rs2(_1_2_steps_rs2));
  jmp_selector _1_6_steps (
    .rs1_val_t_plus_1(_1_2_steps_rs1), .rs2_val_t_plus_1(_1_2_steps_rs2),
    .InstSubType(_2_steps_2_instsubype), .imm(_2_steps_2_imm), .JmpType(_2_steps_2_jmptype),
    .PC(_2_steps_addr), .Nxt(_1_6_steps_nxt), .Jmp_val(_1_6_steps_jmp_val));
  RAMDualPort #(.AddrBits(24), .Bits(8)) ramdualport_1 (
    .A(_7_13_steps_a_ram), .Din(_7_13_steps_din_ram), .str(ON_OFF), .C(_7_13_steps_c_ram),
    .ld(_7_13_steps_ld_ram), .D(ramdualport_1_d));
  assign or_1_out = _7_13_steps_d | _4_steps_d;  // Or or_1, 32 bits wide
  or or_2 (or_2_out, _7_13_steps_c, _4_steps_c);
  assign or_3_out = _7_13_steps_reg | _4_steps_reg;  // Or or_3, 5 bits wide

  // Other names for the same wires on the sheet: pwr = ON_OFF

  // Notes on the sheet:
  //   contents of ROM (hex, n*v repeats v):
  //   b7,10,0,0,13,d1,90,0,b3,d0,20,0,63,8,1,0,b3,81,30,0,13,1,f1,ff
  //   ,6f,f0,5f,ff,17,2,0,0,23,18,32
endmodule
