// Digital circuit decoder.dig as structural Verilog
module decoder (
  input  [31:0] Val,
  input  C,
  input  Pwr,
  output Done,
  output Error,
  output [4:0] Inst,
  output [3:0] InstType,
  output [2:0] InstSubype,
  output InstSubSubType,
  output [4:0] rd,
  output [4:0] rs1,
  output [4:0] shamt_rs2,
  output [31:0] imm,
  output [3:0] JmpType
);

  wire delay_1_out, delay_3_out, has_subsubtype_d, nand_1_out;
  wire [2:0] multiplexer_9_out;
  wire [3:0] type_decoder_2_d, type_decoder_d;
  wire [4:0] delay_2_out, multiplexer_1_out, multiplexer_2_out, multiplexer_3_out;
  wire [11:0] bitextender_1_out;
  wire [19:0] bitextender_2_out;
  wire [20:0] bitextender_3_out;
  wire [31:0] multiplexer_4_out, multiplexer_5_out, multiplexer_6_out, multiplexer_7_out, multiplexer_8_out;

  BitExtender #(.inputBits(1), .outputBits(12)) bitextender_1 (.in(Val[31]), .out(bitextender_1_out));
  BitExtender #(.inputBits(12), .outputBits(20)) bitextender_2 (.in(bitextender_1_out), .out(bitextender_2_out));
  BitExtender #(.inputBits(20), .outputBits(21)) bitextender_3 (.in(bitextender_2_out), .out(bitextender_3_out));
  nand nand_1 (nand_1_out, Val[0], Val[1]);
  ROM #(.AddrBits(5), .Bits(4)) type_decoder (.A(Val[6:2]), .sel(C), .D(type_decoder_d));
  ROM #(.AddrBits(5), .Bits(4)) type_decoder_2 (.A(Val[6:2]), .sel(C), .D(type_decoder_2_d));
  ROM #(.AddrBits(5)) has_subsubtype (.A(Val[6:2]), .sel(C), .D(has_subsubtype_d));
  Multiplexer #(.Bits(5)) multiplexer_1 (.sel(C), .in_0({5{1'b0}}), .in_1(Val[11:7]), .out(multiplexer_1_out));
  Multiplexer #(.Bits(5)) multiplexer_2 (.sel(C), .in_0({5{1'b0}}), .in_1(Val[19:15]), .out(multiplexer_2_out));
  Multiplexer #(.Bits(5)) multiplexer_3 (.sel(C), .in_0({5{1'b0}}), .in_1(Val[24:20]), .out(multiplexer_3_out));
  Multiplexer #(.Bits(32)) multiplexer_4 (
    .sel(C), .in_0({32{1'b0}}), .in_1({bitextender_1_out, Val[19:12], Val[20], Val[30:21], 1'b0}),
    .out(multiplexer_4_out));
  Multiplexer #(.Bits(32)) multiplexer_5 (
    .sel(C), .in_0({32{1'b0}}), .in_1({Val[31:12], {12{1'b0}}}), .out(multiplexer_5_out));
  Multiplexer #(.Bits(32)) multiplexer_6 (
    .sel(C), .in_0({32{1'b0}}), .in_1({bitextender_3_out, Val[30:20]}), .out(multiplexer_6_out));
  Multiplexer #(.Bits(32)) multiplexer_7 (
    .sel(C), .in_0({32{1'b0}}), .in_1({bitextender_3_out, Val[30:25], Val[11:7]}), .out(multiplexer_7_out));
  Multiplexer #(.Bits(32)) multiplexer_8 (
    .sel(C), .in_0({32{1'b0}}), .in_1({bitextender_2_out, Val[7], Val[30:25], Val[11:8], 1'b0}),
    .out(multiplexer_8_out));
  Delay delay_1 (.in(C), .out(delay_1_out));
  Delay #(.Bits(5)) delay_2 (.in(Val[6:2]), .out(delay_2_out));
  Multiplexer #(.Bits(3)) multiplexer_9 (.sel(C), .in_0(3'b000), .in_1(Val[14:12]), .out(multiplexer_9_out));
  Delay delay_3 (.in(Val[30]), .out(delay_3_out));
  and and_1 (Done, Pwr, delay_1_out);
  and and_2 (Error, delay_1_out, nand_1_out);
  Multiplexer #(.Bits(4)) multiplexer_10 (.sel(delay_1_out), .in_0(4'b0000), .in_1(type_decoder_d), .out(JmpType));
  Multiplexer #(.Bits(5)) multiplexer_11 (.sel(delay_1_out), .in_0({5{1'b0}}), .in_1(delay_2_out), .out(Inst));
  Multiplexer #(.Bits(4)) multiplexer_12 (.sel(delay_1_out), .in_0(4'b0000), .in_1(type_decoder_2_d), .out(InstType));
  Multiplexer #(.Selector_Bits(4), .Bits(3)) multiplexer_13 (
    .sel(type_decoder_2_d), .in_0(3'b000), .in_1(3'b000), .in_2(3'b000), .in_3(3'b000),
    .in_4(multiplexer_9_out), .in_5(multiplexer_9_out), .in_6(multiplexer_9_out), .in_7(multiplexer_9_out),
    .in_8(multiplexer_9_out), .in_9(multiplexer_9_out), .in_10(3'b000), .in_11(3'b000), .in_12(3'b000),
    .in_13(3'b000), .in_14(3'b000), .in_15(3'b000), .out(InstSubype));
  Multiplexer multiplexer_14 (.sel(has_subsubtype_d), .in_0(1'b0), .in_1(delay_3_out), .out(InstSubSubType));
  Multiplexer #(.Selector_Bits(4), .Bits(5)) multiplexer_15 (
    .sel(type_decoder_2_d), .in_0({5{1'b0}}), .in_1(multiplexer_1_out), .in_2(multiplexer_1_out),
    .in_3(multiplexer_1_out), .in_4(multiplexer_1_out), .in_5({5{1'b0}}), .in_6(multiplexer_1_out),
    .in_7({5{1'b0}}), .in_8(multiplexer_1_out), .in_9(multiplexer_1_out), .in_10({5{1'b0}}),
    .in_11({5{1'b0}}), .in_12({5{1'b0}}), .in_13({5{1'b0}}), .in_14({5{1'b0}}), .in_15({5{1'b0}}), .out(rd));
  Multiplexer #(.Selector_Bits(4), .Bits(5)) multiplexer_16 (
    .sel(type_decoder_2_d), .in_0({5{1'b0}}), .in_1({5{1'b0}}), .in_2({5{1'b0}}), .in_3(multiplexer_2_out),
    .in_4(multiplexer_2_out), .in_5(multiplexer_2_out), .in_6(multiplexer_2_out), .in_7(multiplexer_2_out),
    .in_8(multiplexer_2_out), .in_9(multiplexer_2_out), .in_10({5{1'b0}}), .in_11({5{1'b0}}),
    .in_12({5{1'b0}}), .in_13({5{1'b0}}), .in_14({5{1'b0}}), .in_15({5{1'b0}}), .out(rs1));
  Multiplexer #(.Selector_Bits(4), .Bits(5)) multiplexer_17 (
    .sel(type_decoder_2_d), .in_0({5{1'b0}}), .in_1({5{1'b0}}), .in_2({5{1'b0}}), .in_3({5{1'b0}}),
    .in_4({5{1'b0}}), .in_5(multiplexer_3_out), .in_6({5{1'b0}}), .in_7(multiplexer_3_out),
    .in_8(multiplexer_3_out), .in_9(multiplexer_3_out), .in_10({5{1'b0}}), .in_11({5{1'b0}}),
    .in_12({5{1'b0}}), .in_13({5{1'b0}}), .in_14({5{1'b0}}), .in_15({5{1'b0}}), .out(shamt_rs2));
  Multiplexer #(.Selector_Bits(4), .Bits(32)) multiplexer_18 (
    .sel(type_decoder_2_d), .in_0({32{1'b0}}), .in_1(multiplexer_5_out), .in_2(multiplexer_5_out),
    .in_3(multiplexer_4_out), .in_4(multiplexer_6_out), .in_5(multiplexer_8_out), .in_6(multiplexer_6_out),
    .in_7(multiplexer_7_out), .in_8(multiplexer_6_out), .in_9({32{1'b0}}), .in_10({32{1'b0}}),
    .in_11({32{1'b0}}), .in_12({32{1'b0}}), .in_13({32{1'b0}}), .in_14({32{1'b0}}), .in_15({32{1'b0}}),
    .out(imm));

  // Notes on the sheet:
  //   InstType: 0: error, 
  //   1: lui, 
  //   2: auipc, 
  //   3: jal, 
  //   4: jalr,
  //   5: Branch, 
  //   6: load, 
  //   7: store, 
  //   8: ALU imm,
  //   9: ALU reg,
  //   Instruction
  //   Instruction
  //   subtype
  //   Instruction
  //   subsubtype
  //   rd
  //   rs1
  //   rs2
  //   shamt
  //   imm_ujibs 10:5
  //   imm_bs 4:1
  //   imm_s 4:0
  //   imm_ju 19:12
  //   imm_bi 10:1
  //   imm_j
  //   imm_u
  //   imm_i
  //   imm_s
  //   imm_b
  //   contents of type_decoder (hex, n*v repeats v):
  //   24*1,8,4,1,2,4*1
  //   contents of type_decoder_2 (hex, n*v repeats v):
  //   6,0,0,0,8,2,0,0,7,0,0,0,9,1,10*0,5,4,0,3
  //   contents of has_subsubtype (hex, n*v repeats v):
  //   4*0,1,7*0,1
endmodule
