// Digital circuit jmp_selector.dig as structural Verilog
module jmp_selector (
  input  [31:0] rs1_val_t_plus_1,
  input  [31:0] rs2_val_t_plus_1,
  input  [2:0] InstSubType,
  input  [31:0] imm,
  input  [3:0] JmpType,
  input  [31:0] PC,
  output Nxt,
  output [31:0] Jmp_val
);

  wire delay_9_out, delay_10_out, delay_11_out, delay_12_out, delay_13_out, multiplexer_3_out, not_1_out,
       Signed_eq, Signed_gt, Signed_lt, Unsigned_gt, Unsigned_lt;
  wire [2:0] delay_5_out, delay_7_out, delay_8_out;
  wire [3:1] delay_3_out;
  wire [31:0] delay_4_out, delay_6_out, jal_s, jalr_s, multiplexer_1_out, PC_plus_4_s;

  Delay delay_1 (.in(JmpType[1]), .out(delay_3_out[1]));
  Delay #(.delayTime(2)) delay_2 (.in(JmpType[2]), .out(delay_3_out[2]));
  Delay #(.delayTime(5)) delay_3 (.in(JmpType[3]), .out(delay_3_out[3]));
  Add #(.Bits(32)) jal (.a(imm), .b(PC), .c_i(1'b0), .s(jal_s));  // open: c_o
  Add #(.Bits(32)) PC_plus_4 (.a(32'h4), .b(PC), .c_i(1'b0), .s(PC_plus_4_s));  // open: c_o
  Delay #(.Bits(32)) delay_4 (.in(imm), .out(delay_4_out));
  Delay #(.Bits(3)) delay_5 (.in(InstSubType), .out(delay_5_out));
  Delay #(.Bits(32), .delayTime(3)) delay_6 (.in(jal_s), .out(delay_6_out));
  Multiplexer #(.Bits(32)) multiplexer_1 (
    .sel(multiplexer_3_out), .in_0(PC_plus_4_s), .in_1(delay_6_out), .out(multiplexer_1_out));
  Add #(.Bits(32)) jalr (.a(delay_4_out), .b(rs1_val_t_plus_1), .c_i(1'b0), .s(jalr_s));  // open: c_o
  Delay #(.Bits(3)) delay_7 (.in(delay_5_out), .out(delay_7_out));
  Comparator #(.Signed("true"), .Bits(32)) Signed (
    .a(rs1_val_t_plus_1), .b(rs2_val_t_plus_1), .gt(Signed_gt), .eq(Signed_eq), .lt(Signed_lt));
  Comparator #(.Bits(32)) Unsigned (
    .a(rs1_val_t_plus_1), .b(rs2_val_t_plus_1), .gt(Unsigned_gt), .lt(Unsigned_lt));  // open: eq
  PriorityEncoder #(.Selector_Bits(2)) priorityencoder_1 (
    .in0(JmpType[0]), .in1(delay_3_out[1]), .in2(delay_3_out[2]), .in3(delay_3_out[3]), .any(Nxt));  // open: num
  Multiplexer #(.Selector_Bits(4), .Bits(32)) multiplexer_2 (
    .sel({delay_3_out, JmpType[0]}), .in_0(PC_plus_4_s), .in_1(PC_plus_4_s), .in_2(jal_s),
    .in_3(PC_plus_4_s), .in_4(jalr_s), .in_5(PC_plus_4_s), .in_6(PC_plus_4_s), .in_7(PC_plus_4_s),
    .in_8(multiplexer_1_out), .in_9(PC_plus_4_s), .in_10(PC_plus_4_s), .in_11(PC_plus_4_s),
    .in_12(PC_plus_4_s), .in_13(PC_plus_4_s), .in_14(PC_plus_4_s), .in_15(PC_plus_4_s), .out(Jmp_val));
  Delay #(.Bits(3)) delay_8 (.in(delay_7_out), .out(delay_8_out));
  Delay delay_9 (.in(Signed_eq), .out(delay_9_out));
  not not_1 (not_1_out, Signed_eq);
  Delay delay_10 (.in(Signed_lt), .out(delay_10_out));
  Delay delay_11 (.in(Signed_gt), .out(delay_11_out));
  Delay delay_12 (.in(Unsigned_lt), .out(delay_12_out));
  Delay delay_13 (.in(Unsigned_gt), .out(delay_13_out));
  Multiplexer #(.Selector_Bits(3)) multiplexer_3 (
    .sel(delay_8_out), .in_0(delay_9_out), .in_1(not_1_out), .in_2(1'b0), .in_3(1'b0), .in_4(delay_10_out),
    .in_5(delay_11_out), .in_6(delay_12_out), .in_7(delay_13_out), .out(multiplexer_3_out));

  // Notes on the sheet:
  //   JmpType: 1: next, PC+4 (t+1)
  //   2: jal, PC+imm (t+2)
  //   4: jalr, PC+rs1 (t+3)
  //   8: conditional branch, PC+imm else PC+4 (t+6)
  //   Branch decision making
endmodule
