// Digital circuit pulse.dig as structural Verilog
module pulse (
  input  In,
  output Out
);

  wire delay_1_out;

  Delay #(.generic("this.delayTime=args.Duration;")) delay_1 (.in(In), .out(delay_1_out));
  RS_FF_AS rs_ff_as_1 (.S(In), .R(delay_1_out), .Q(Out));  // open: nQ
endmodule

/* Code that sets the parameters or builds the circuit:
Duration := 4;
*/
