// Digital circuit registers.dig as structural Verilog
module registers (
  input  [4:0] Reg,
  input  [31:0] D,
  input  C,
  input  [4:0] rs1_sel,
  input  [4:0] rs2_sel,
  input  Rst,
  input  Pwr,
  output [31:0] rs1,
  output [31:0] rs2
);

  wire demultiplexer_1_out_1, demultiplexer_1_out_2, demultiplexer_1_out_3, demultiplexer_1_out_4,
       demultiplexer_1_out_5, demultiplexer_1_out_6, demultiplexer_1_out_7, demultiplexer_1_out_8,
       demultiplexer_1_out_9, demultiplexer_1_out_10, demultiplexer_1_out_11, demultiplexer_1_out_12,
       demultiplexer_1_out_13, demultiplexer_1_out_14, demultiplexer_1_out_15, demultiplexer_1_out_16,
       demultiplexer_1_out_17, demultiplexer_1_out_18, demultiplexer_1_out_19, demultiplexer_1_out_20,
       demultiplexer_1_out_21, demultiplexer_1_out_22, demultiplexer_1_out_23, demultiplexer_1_out_24,
       demultiplexer_1_out_25, demultiplexer_1_out_26, demultiplexer_1_out_27, demultiplexer_1_out_28,
       demultiplexer_1_out_29, demultiplexer_1_out_30, demultiplexer_1_out_31, or_1_out;
  wire [4:0] delay_1_out;
  wire [31:0] d_t, multiplexer_1_out, x01_q, x2_q, x3_q, x4_q, x5_q, x6_q, x7_q, x8_q, x9_q, x10_q, x11_q,
       x12_q, x13_q, x14_q, x15_q, x16_q, x17_q, x18_q, x19_q, x20_q, x21_q, x22_q, x23_q, x24_q, x25_q,
       x26_q, x27_q, x28_q, x29_q, x30_q, x31_q;

  Delay #(.Bits(5)) delay_1 (.in(Reg), .out(delay_1_out));
  or or_1 (or_1_out, C, Rst);
  Multiplexer #(.Bits(32)) multiplexer_1 (.sel(Rst), .in_0(D), .in_1({32{1'b0}}), .out(multiplexer_1_out));
  Demultiplexer #(.Selector_Bits(5)) demultiplexer_1 (
    .sel(delay_1_out), .in(or_1_out), .out_1(demultiplexer_1_out_1), .out_2(demultiplexer_1_out_2),
    .out_3(demultiplexer_1_out_3), .out_4(demultiplexer_1_out_4), .out_5(demultiplexer_1_out_5),
    .out_6(demultiplexer_1_out_6), .out_7(demultiplexer_1_out_7), .out_8(demultiplexer_1_out_8),
    .out_9(demultiplexer_1_out_9), .out_10(demultiplexer_1_out_10), .out_11(demultiplexer_1_out_11),
    .out_12(demultiplexer_1_out_12), .out_13(demultiplexer_1_out_13), .out_14(demultiplexer_1_out_14),
    .out_15(demultiplexer_1_out_15), .out_16(demultiplexer_1_out_16), .out_17(demultiplexer_1_out_17),
    .out_18(demultiplexer_1_out_18), .out_19(demultiplexer_1_out_19), .out_20(demultiplexer_1_out_20),
    .out_21(demultiplexer_1_out_21), .out_22(demultiplexer_1_out_22), .out_23(demultiplexer_1_out_23),
    .out_24(demultiplexer_1_out_24), .out_25(demultiplexer_1_out_25), .out_26(demultiplexer_1_out_26),
    .out_27(demultiplexer_1_out_27), .out_28(demultiplexer_1_out_28), .out_29(demultiplexer_1_out_29),
    .out_30(demultiplexer_1_out_30), .out_31(demultiplexer_1_out_31));  // open: out_0
  Delay #(.Bits(32)) delay_2 (.in(multiplexer_1_out), .out(d_t));
  Register #(.Bits(32)) x01 (.D(d_t), .C(demultiplexer_1_out_1), .en(Pwr), .Q(x01_q));
  Register #(.Bits(32)) x2 (.D(d_t), .C(demultiplexer_1_out_2), .en(Pwr), .Q(x2_q));
  Register #(.Bits(32)) x3 (.D(d_t), .C(demultiplexer_1_out_3), .en(Pwr), .Q(x3_q));
  Register #(.Bits(32)) x4 (.D(d_t), .C(demultiplexer_1_out_4), .en(Pwr), .Q(x4_q));
  Register #(.Bits(32)) x5 (.D(d_t), .C(demultiplexer_1_out_5), .en(Pwr), .Q(x5_q));
  Register #(.Bits(32)) x6 (.D(d_t), .C(demultiplexer_1_out_6), .en(Pwr), .Q(x6_q));
  Register #(.Bits(32)) x7 (.D(d_t), .C(demultiplexer_1_out_7), .en(Pwr), .Q(x7_q));
  Register #(.Bits(32)) x8 (.D(d_t), .C(demultiplexer_1_out_8), .en(Pwr), .Q(x8_q));
  Register #(.Bits(32)) x9 (.D(d_t), .C(demultiplexer_1_out_9), .en(Pwr), .Q(x9_q));
  Register #(.Bits(32)) x10 (.D(d_t), .C(demultiplexer_1_out_10), .en(Pwr), .Q(x10_q));
  Register #(.Bits(32)) x11 (.D(d_t), .C(demultiplexer_1_out_11), .en(Pwr), .Q(x11_q));
  Register #(.Bits(32)) x12 (.D(d_t), .C(demultiplexer_1_out_12), .en(Pwr), .Q(x12_q));
  Register #(.Bits(32)) x13 (.D(d_t), .C(demultiplexer_1_out_13), .en(Pwr), .Q(x13_q));
  Register #(.Bits(32)) x14 (.D(d_t), .C(demultiplexer_1_out_14), .en(Pwr), .Q(x14_q));
  Register #(.Bits(32)) x15 (.D(d_t), .C(demultiplexer_1_out_15), .en(Pwr), .Q(x15_q));
  Register #(.Bits(32)) x16 (.D(d_t), .C(demultiplexer_1_out_16), .en(Pwr), .Q(x16_q));
  Register #(.Bits(32)) x17 (.D(d_t), .C(demultiplexer_1_out_17), .en(Pwr), .Q(x17_q));
  Register #(.Bits(32)) x18 (.D(d_t), .C(demultiplexer_1_out_18), .en(Pwr), .Q(x18_q));
  Register #(.Bits(32)) x19 (.D(d_t), .C(demultiplexer_1_out_19), .en(Pwr), .Q(x19_q));
  Register #(.Bits(32)) x20 (.D(d_t), .C(demultiplexer_1_out_20), .en(Pwr), .Q(x20_q));
  Register #(.Bits(32)) x21 (.D(d_t), .C(demultiplexer_1_out_21), .en(Pwr), .Q(x21_q));
  Register #(.Bits(32)) x22 (.D(d_t), .C(demultiplexer_1_out_22), .en(Pwr), .Q(x22_q));
  Register #(.Bits(32)) x23 (.D(d_t), .C(demultiplexer_1_out_23), .en(Pwr), .Q(x23_q));
  Register #(.Bits(32)) x24 (.D(d_t), .C(demultiplexer_1_out_24), .en(Pwr), .Q(x24_q));
  Register #(.Bits(32)) x25 (.D(d_t), .C(demultiplexer_1_out_25), .en(Pwr), .Q(x25_q));
  Register #(.Bits(32)) x26 (.D(d_t), .C(demultiplexer_1_out_26), .en(Pwr), .Q(x26_q));
  Register #(.Bits(32)) x27 (.D(d_t), .C(demultiplexer_1_out_27), .en(Pwr), .Q(x27_q));
  Register #(.Bits(32)) x28 (.D(d_t), .C(demultiplexer_1_out_28), .en(Pwr), .Q(x28_q));
  Register #(.Bits(32)) x29 (.D(d_t), .C(demultiplexer_1_out_29), .en(Pwr), .Q(x29_q));
  Register #(.Bits(32)) x30 (.D(d_t), .C(demultiplexer_1_out_30), .en(Pwr), .Q(x30_q));
  Register #(.Bits(32)) x31 (.D(d_t), .C(demultiplexer_1_out_31), .en(Pwr), .Q(x31_q));
  Multiplexer #(.Selector_Bits(5), .Bits(32)) multiplexer_2 (
    .sel(rs1_sel), .in_0({32{1'b0}}), .in_1(x01_q), .in_2(x2_q), .in_3(x3_q), .in_4(x4_q), .in_5(x5_q),
    .in_6(x6_q), .in_7(x7_q), .in_8(x8_q), .in_9(x9_q), .in_10(x10_q), .in_11(x11_q), .in_12(x12_q),
    .in_13(x13_q), .in_14(x14_q), .in_15(x15_q), .in_16(x16_q), .in_17(x17_q), .in_18(x18_q), .in_19(x19_q),
    .in_20(x20_q), .in_21(x21_q), .in_22(x22_q), .in_23(x23_q), .in_24(x24_q), .in_25(x25_q), .in_26(x26_q),
    .in_27(x27_q), .in_28(x28_q), .in_29(x29_q), .in_30(x30_q), .in_31(x31_q), .out(rs1));
  Multiplexer #(.Selector_Bits(5), .Bits(32)) multiplexer_3 (
    .sel(rs2_sel), .in_0({32{1'b0}}), .in_1(x01_q), .in_2(x2_q), .in_3(x3_q), .in_4(x4_q), .in_5(x5_q),
    .in_6(x6_q), .in_7(x7_q), .in_8(x8_q), .in_9(x9_q), .in_10(x10_q), .in_11(x11_q), .in_12(x12_q),
    .in_13(x13_q), .in_14(x14_q), .in_15(x15_q), .in_16(x16_q), .in_17(x17_q), .in_18(x18_q), .in_19(x19_q),
    .in_20(x20_q), .in_21(x21_q), .in_22(x22_q), .in_23(x23_q), .in_24(x24_q), .in_25(x25_q), .in_26(x26_q),
    .in_27(x27_q), .in_28(x28_q), .in_29(x29_q), .in_30(x30_q), .in_31(x31_q), .out(rs2));

  // Other names for the same wires on the sheet: rs1_tunnel_reg[4:0] = rs1_sel; rs2_tunnel_reg[4:0] = rs2_sel

  // Notes on the sheet:
  //   rs1
  //   rs2
endmodule
